// Logisim project schematic.circ as structural Verilog: 14 circuits, main circuit main
module main (
);

  wire [15:0] OP1_q, OP2_q;

  RAM #(.addrWidth(16), .dataWidth(16)) ram_1 ();  // open: addr, we, oe, clk, din, dout
  Register #(.width(16)) IR ();  // open: D, en, clk, Q, clr
  Register #(.width(16)) PC ();  // open: D, en, clk, Q, clr
  Register #(.width(16)) OP1 (.Q(OP1_q));  // open: D, en, clk, clr
  Register #(.width(16)) OP2 (.Q(OP2_q));  // open: D, en, clk, clr
  REGFILE REGSFILE ();  // open: REG_STORE, CLK, REG_FETCH_A, REG_FETCH_B, BUS_IN, BUS_A, BUS_B
  ALU alu_1 ();  // open: opA, opB, PREFIX, OPCODE, ALU_OUT, FLAG_OUT
endmodule

module fulladder (
  input  CIN,
  input  A,
  input  B,
  output SUM,
  output COUT
);

  wire and_1_out, and_2_out, xor_1_out;

  xor xor_1 (xor_1_out, A, B);
  and and_1 (and_1_out, B, A);
  xor xor_2 (SUM, CIN, xor_1_out);
  and and_2 (and_2_out, CIN, xor_1_out);
  or or_1 (COUT, and_2_out, and_1_out);
endmodule

module FA_16 (
  input  [15:0] A,
  input  CIN,
  input  [15:0] B,
  output [15:0] SUM,
  output COUT
);

  wire fa_4_1_cout, fa_4_2_cout, fa_4_3_cout;

  FA_4 fa_4_1 (.A(A[3:0]), .B(B[3:0]), .CIN(CIN), .COUT(fa_4_1_cout), .SUM(SUM[3:0]));
  FA_4 fa_4_2 (.A(A[7:4]), .B(B[7:4]), .CIN(fa_4_1_cout), .COUT(fa_4_2_cout), .SUM(SUM[7:4]));
  FA_4 fa_4_3 (.A(A[11:8]), .B(B[11:8]), .CIN(fa_4_2_cout), .COUT(fa_4_3_cout), .SUM(SUM[11:8]));
  FA_4 fa_4_4 (.A(A[15:12]), .B(B[15:12]), .CIN(fa_4_3_cout), .COUT(COUT), .SUM(SUM[15:12]));
endmodule

module FA_4 (
  input  [3:0] A,
  input  CIN,
  input  [3:0] B,
  output [3:0] SUM,
  output COUT
);

  wire fulladder_1_cout, fulladder_2_cout, fulladder_3_cout;

  fulladder fulladder_1 (.A(A[0]), .B(B[0]), .CIN(CIN), .COUT(fulladder_1_cout), .SUM(SUM[0]));
  fulladder fulladder_2 (.A(A[1]), .B(B[1]), .CIN(fulladder_1_cout), .COUT(fulladder_2_cout), .SUM(SUM[1]));
  fulladder fulladder_3 (.A(A[2]), .B(B[2]), .CIN(fulladder_2_cout), .COUT(fulladder_3_cout), .SUM(SUM[2]));
  fulladder fulladder_4 (.A(A[3]), .B(B[3]), .CIN(fulladder_3_cout), .COUT(COUT), .SUM(SUM[3]));
endmodule

module ALU (
  input  [15:0] opA,
  input  [15:0] opB,
  input  [2:0] PREFIX,
  input  [2:0] OPCODE,
  output [15:0] ALU_OUT,
  output [15:0] FLAG_OUT
);

  wire fa_16_1_cout, multiplexer_3_out, multiplexer_5_out, shift_block_1_cout;
  wire [15:0] and_1_out, fa_16_1_sum, multiplexer_1_out, multiplexer_2_out, multiplexer_4_out, not_1_out,
       not_2_out, not_3_out, or_1_out, shift_block_1_asl, shift_block_1_asr, shift_block_1_lsl,
       shift_block_1_lsr, xor_1_out;

  assign not_1_out = ~opB;  // NOT_Gate not_1, 16 bits wide
  Multiplexer #(.select(2), .width(16)) multiplexer_1 (
    .in0(opB), .in1(not_1_out), .in2({16{1'b1}}), .in3({16{1'b0}}), .out(multiplexer_1_out), .sel(OPCODE[1:0]));
  FA_16 fa_16_1 (.B(multiplexer_1_out), .A(opA), .CIN(OPCODE[0]), .COUT(fa_16_1_cout), .SUM(fa_16_1_sum));
  assign and_1_out = opA & opB;  // AND_Gate and_1, 16 bits wide
  assign or_1_out = opA | opB;  // OR_Gate or_1, 16 bits wide
  assign not_2_out = ~opA;  // NOT_Gate not_2, 16 bits wide
  assign xor_1_out = opA ^ opB;  // XOR_Gate xor_1, 16 bits wide
  assign not_3_out = ~xor_1_out;  // NOT_Gate not_3, 16 bits wide
  Multiplexer #(.select(2), .width(16)) multiplexer_2 (
    .in0(and_1_out), .in1(or_1_out), .in2(not_2_out), .in3(not_3_out), .out(multiplexer_2_out),
    .sel(OPCODE[1:0]));
  Multiplexer #(.select(2)) multiplexer_3 (
    .in0(fa_16_1_cout), .in1(1'b0), .in2(shift_block_1_cout), .in3(1'b0), .out(multiplexer_3_out),
    .sel(PREFIX[1:0]));
  Shift_Block shift_block_1 (
    .SHIFTER(opA), .LSL(shift_block_1_lsl), .LSR(shift_block_1_lsr), .ASL(shift_block_1_asl),
    .ASR(shift_block_1_asr), .COUT(shift_block_1_cout));
  Multiplexer #(.select(2), .width(16)) multiplexer_4 (
    .in0(shift_block_1_lsl), .in1(shift_block_1_lsr), .in2(shift_block_1_asl), .in3(shift_block_1_asr),
    .out(multiplexer_4_out), .sel(OPCODE[1:0]));
  Multiplexer #(.select(2)) multiplexer_5 (
    .in0(OPCODE[0]), .in1(1'b0), .in2(1'b0), .in3(1'b0), .out(multiplexer_5_out), .sel(PREFIX[1:0]));
  Multiplexer #(.select(2), .width(16)) multiplexer_6 (
    .in0({16{1'b1}}), .in1(fa_16_1_sum), .in2(multiplexer_2_out), .in3(multiplexer_4_out), .out(ALU_OUT),
    .sel(PREFIX[1:0]));
  flagdesignation flagdesignation_1 (
    .CARRYIN(multiplexer_5_out), .CARRYOUT(multiplexer_3_out), .in_3(ALU_OUT), .out_4(FLAG_OUT));

  // Notes on the sheet:
  //   prefix muxes output
  //   Legal Prefixes:
  //   arith out
  //   001 - Arithmetic Ops
  //   000 - ADD AB
  //   001 - SUB AB
  //   010 - DEC A
  //   011 - INC A
  //   010 - Logic Ops
  //   000 - AND AB
  //   001 - ORR AB
  //   010 - NOT A
  //   011 - EQL AB
  //   logic out
  //   shift out
  //   011 - Shift Ops
  //   000 - LSL A
  //   001 - LSR A
  //   010 - ASL A
  //   011 - ASR A
endmodule

module Shift_Block (
  input  [15:0] SHIFTER,
  output [15:0] LSL,
  output [15:0] LSR,
  output COUT,
  output [15:0] ASL,
  output [15:0] ASR
);

  wire or_1_out, or_2_out;

  or or_1 (or_1_out, SHIFTER[15], SHIFTER[0]);
  or or_2 (or_2_out, SHIFTER[15], SHIFTER[0]);
  or or_3 (COUT, or_1_out, or_2_out);

  assign ASL = {SHIFTER[14:0], SHIFTER[0]};
  assign ASR = {{2{SHIFTER[15]}}, SHIFTER[14:1]};
  assign LSL = {SHIFTER[14:0], 1'b0};
  assign LSR = {SHIFTER[0], SHIFTER[15:1]};

  // Notes on the sheet:
  //   LSL // LSR // ASL // ASR
endmodule

module flagdesignation (
  input  CARRYIN,
  input  CARRYOUT,
  input  [15:0] in_3,
  output [15:0] out_4
);

  xor xor_1 (out_4[2], CARRYIN, CARRYOUT);
  nor nor_1 (out_4[0], in_3[0], in_3[1], in_3[2], in_3[3], in_3[4], in_3[5], in_3[6], in_3[7], in_3[8], in_3[9], in_3[10], in_3[11], in_3[12], in_3[13], in_3[14], in_3[15]);

  assign {out_4[15:3], out_4[1]} = {{12{1'b0}}, in_3[15], in_3[0]};

  // Notes on the sheet:
  //   zero // even parity (high on odd value) // overflow // negative
endmodule

module reg1 (
  input  DATA_IN,
  input  STORE_BAR,
  input  CLOCK,
  output VALUE
);

  wire and_1_out, and_2_out, nand_1_out, nand_2_out, nand_4_out, not_1_out, not_2_out, not_3_out, not_4_out,
       not_5_out;

  not not_1 (not_1_out, CLOCK);
  not not_2 (not_2_out, STORE_BAR);
  not not_3 (not_3_out, not_1_out);
  not not_4 (not_4_out, not_3_out);
  and and_1 (and_1_out, not_2_out, and_2_out);
  and and_2 (and_2_out, CLOCK, not_4_out);
  not not_5 (not_5_out, DATA_IN);
  nand nand_1 (nand_1_out, DATA_IN, and_1_out);
  nand nand_2 (nand_2_out, and_1_out, not_5_out);
  LED led_1 (.in(VALUE));
  nand nand_3 (VALUE, nand_1_out, nand_4_out);
  nand nand_4 (nand_4_out, VALUE, nand_2_out);
endmodule

module reg16 (
  input  [15:0] DATA_IN,
  input  STORE,
  input  CLK,
  output [15:0] VALUE
);

  wire not_1_out;

  not not_1 (not_1_out, STORE);
  reg1 reg1_1 (.CLOCK(CLK), .STORE_BAR(not_1_out), .DATA_IN(DATA_IN[0]), .VALUE(VALUE[0]));
  reg1 reg1_2 (.CLOCK(CLK), .STORE_BAR(not_1_out), .DATA_IN(DATA_IN[1]), .VALUE(VALUE[1]));
  reg1 reg1_3 (.CLOCK(CLK), .STORE_BAR(not_1_out), .DATA_IN(DATA_IN[2]), .VALUE(VALUE[2]));
  reg1 reg1_4 (.CLOCK(CLK), .STORE_BAR(not_1_out), .DATA_IN(DATA_IN[3]), .VALUE(VALUE[3]));
  reg1 reg1_5 (.CLOCK(CLK), .STORE_BAR(not_1_out), .DATA_IN(DATA_IN[4]), .VALUE(VALUE[4]));
  reg1 reg1_6 (.CLOCK(CLK), .STORE_BAR(not_1_out), .DATA_IN(DATA_IN[5]), .VALUE(VALUE[5]));
  reg1 reg1_7 (.CLOCK(CLK), .STORE_BAR(not_1_out), .DATA_IN(DATA_IN[6]), .VALUE(VALUE[6]));
  reg1 reg1_8 (.CLOCK(CLK), .STORE_BAR(not_1_out), .DATA_IN(DATA_IN[7]), .VALUE(VALUE[7]));
  reg1 reg1_9 (.CLOCK(CLK), .STORE_BAR(not_1_out), .DATA_IN(DATA_IN[8]), .VALUE(VALUE[8]));
  reg1 reg1_10 (.CLOCK(CLK), .STORE_BAR(not_1_out), .DATA_IN(DATA_IN[9]), .VALUE(VALUE[9]));
  reg1 reg1_11 (.CLOCK(CLK), .STORE_BAR(not_1_out), .DATA_IN(DATA_IN[10]), .VALUE(VALUE[10]));
  reg1 reg1_12 (.CLOCK(CLK), .STORE_BAR(not_1_out), .DATA_IN(DATA_IN[11]), .VALUE(VALUE[11]));
  reg1 reg1_13 (.CLOCK(CLK), .STORE_BAR(not_1_out), .DATA_IN(DATA_IN[12]), .VALUE(VALUE[12]));
  reg1 reg1_14 (.CLOCK(CLK), .STORE_BAR(not_1_out), .DATA_IN(DATA_IN[13]), .VALUE(VALUE[13]));
  reg1 reg1_15 (.CLOCK(CLK), .STORE_BAR(not_1_out), .DATA_IN(DATA_IN[14]), .VALUE(VALUE[14]));
  reg1 reg1_16 (.CLOCK(CLK), .STORE_BAR(not_1_out), .DATA_IN(DATA_IN[15]), .VALUE(VALUE[15]));
  Hex_Digit_Display HIGHEST (.value(VALUE[15:12]));  // open: dp
  Hex_Digit_Display HIGH (.value(VALUE[11:8]));  // open: dp
  Hex_Digit_Display LOW (.value(VALUE[7:4]));  // open: dp
  Hex_Digit_Display LOWEST (.value(VALUE[3:0]));  // open: dp
endmodule

module REGFILE (
  input  [15:0] BUS_IN,
  input  [2:0] REG_STORE,
  input  CLK,
  input  [2:0] REG_FETCH_A,
  input  [2:0] REG_FETCH_B,
  output [15:0] BUS_A,
  output [15:0] BUS_B
);

  wire decoder_1_out0, decoder_1_out1, decoder_1_out2, decoder_1_out3, decoder_1_out4, decoder_1_out5,
       decoder_1_out6, decoder_1_out7;
  wire [15:0] REG_A_value, REG_B_value, REG_C_value, REG_D_value, REG_F_value, REG_J_value, REG_S_value,
       REG_W_value;

  Decoder #(.enable("false"), .select(3)) decoder_1 (
    .out0(decoder_1_out0), .out1(decoder_1_out1), .out2(decoder_1_out2), .out3(decoder_1_out3),
    .out4(decoder_1_out4), .out5(decoder_1_out5), .out6(decoder_1_out6), .out7(decoder_1_out7),
    .sel(REG_STORE));
  reg16 REG_A (.DATA_IN(BUS_IN), .STORE(decoder_1_out0), .CLK(CLK), .VALUE(REG_A_value));
  reg16 REG_S (.DATA_IN(BUS_IN), .STORE(decoder_1_out4), .CLK(CLK), .VALUE(REG_S_value));
  reg16 REG_B (.DATA_IN(BUS_IN), .STORE(decoder_1_out1), .CLK(CLK), .VALUE(REG_B_value));
  reg16 REG_F (.DATA_IN(BUS_IN), .STORE(decoder_1_out5), .CLK(CLK), .VALUE(REG_F_value));
  reg16 REG_C (.DATA_IN(BUS_IN), .STORE(decoder_1_out2), .CLK(CLK), .VALUE(REG_C_value));
  reg16 REG_W (.DATA_IN(BUS_IN), .STORE(decoder_1_out6), .CLK(CLK), .VALUE(REG_W_value));
  reg16 REG_D (.DATA_IN(BUS_IN), .STORE(decoder_1_out3), .CLK(CLK), .VALUE(REG_D_value));
  reg16 REG_J (.DATA_IN(BUS_IN), .STORE(decoder_1_out7), .CLK(CLK), .VALUE(REG_J_value));
  Multiplexer #(.select(3), .width(16)) multiplexer_1 (
    .in0(REG_A_value), .in1(REG_B_value), .in2(REG_C_value), .in3(REG_D_value), .in4(REG_S_value),
    .in5(REG_F_value), .in6(REG_W_value), .in7(REG_J_value), .out(BUS_A), .sel(REG_FETCH_A));
  Multiplexer #(.select(3), .width(16)) multiplexer_2 (
    .in0(REG_A_value), .in1(REG_B_value), .in2(REG_C_value), .in3(REG_D_value), .in4(REG_S_value),
    .in5(REG_F_value), .in6(REG_W_value), .in7(REG_J_value), .out(BUS_B), .sel(REG_FETCH_B));
endmodule

module INSTRUCTION_DECODER (
  input  [15:0] PC_IN,
  input  in_2
);

  wire [15:0] incrementor_1_16_1_val_out, incrementor_2_16_1_val_out;

  INCREMENTOR_1_16 incrementor_1_16_1 (.VAL_IN(PC_IN), .VAL_OUT(incrementor_1_16_1_val_out));
  INCREMENTOR_2_16 incrementor_2_16_1 (.VAL_IN(PC_IN), .VAL_OUT(incrementor_2_16_1_val_out));

  // Notes on the sheet:
  //   Load PC + 0 into IR
  //   Load PC + 1 into OP1R
  //   Load PC + 2 into OP2R
  //   Pass I-Value into PC
endmodule

module INCREMENTOR_1_16 (
  input  [15:0] VAL_IN,
  output [15:0] VAL_OUT
);

  wire halfadder_1_c, halfadder_2_c, halfadder_3_c, halfadder_4_c, halfadder_5_c, halfadder_6_c,
       halfadder_7_c, halfadder_8_c, halfadder_9_c, halfadder_10_c, halfadder_11_c, halfadder_12_c,
       halfadder_13_c, halfadder_14_c, halfadder_15_c;

  halfadder halfadder_1 (.A(VAL_IN[0]), .B(1'b1), .S(VAL_OUT[0]), .C(halfadder_1_c));
  halfadder halfadder_2 (.A(VAL_IN[1]), .B(halfadder_1_c), .S(VAL_OUT[1]), .C(halfadder_2_c));
  halfadder halfadder_3 (.A(VAL_IN[2]), .B(halfadder_2_c), .S(VAL_OUT[2]), .C(halfadder_3_c));
  halfadder halfadder_4 (.A(VAL_IN[3]), .B(halfadder_3_c), .S(VAL_OUT[3]), .C(halfadder_4_c));
  halfadder halfadder_5 (.A(VAL_IN[4]), .B(halfadder_4_c), .S(VAL_OUT[4]), .C(halfadder_5_c));
  halfadder halfadder_6 (.A(VAL_IN[5]), .B(halfadder_5_c), .S(VAL_OUT[5]), .C(halfadder_6_c));
  halfadder halfadder_7 (.A(VAL_IN[6]), .B(halfadder_6_c), .S(VAL_OUT[6]), .C(halfadder_7_c));
  halfadder halfadder_8 (.A(VAL_IN[7]), .B(halfadder_7_c), .S(VAL_OUT[7]), .C(halfadder_8_c));
  halfadder halfadder_9 (.A(VAL_IN[8]), .B(halfadder_8_c), .S(VAL_OUT[8]), .C(halfadder_9_c));
  halfadder halfadder_10 (.A(VAL_IN[9]), .B(halfadder_9_c), .S(VAL_OUT[9]), .C(halfadder_10_c));
  halfadder halfadder_11 (.A(VAL_IN[10]), .B(halfadder_10_c), .S(VAL_OUT[10]), .C(halfadder_11_c));
  halfadder halfadder_12 (.A(VAL_IN[11]), .B(halfadder_11_c), .S(VAL_OUT[11]), .C(halfadder_12_c));
  halfadder halfadder_13 (.A(VAL_IN[12]), .B(halfadder_12_c), .S(VAL_OUT[12]), .C(halfadder_13_c));
  halfadder halfadder_14 (.A(VAL_IN[13]), .B(halfadder_13_c), .S(VAL_OUT[13]), .C(halfadder_14_c));
  halfadder halfadder_15 (.A(VAL_IN[14]), .B(halfadder_14_c), .S(VAL_OUT[14]), .C(halfadder_15_c));
  halfadder halfadder_16 (.A(VAL_IN[15]), .B(halfadder_15_c), .S(VAL_OUT[15]));  // open: C
endmodule

module halfadder (
  input  B,
  input  A,
  output S,
  output C
);

  xor xor_1 (S, B, A);
  and and_1 (C, A, B);
endmodule

module INCREMENTOR_2_16 (
  input  [15:0] VAL_IN,
  output [15:0] VAL_OUT
);

  wire halfadder_1_c, halfadder_2_c, halfadder_3_c, halfadder_4_c, halfadder_5_c, halfadder_6_c,
       halfadder_7_c, halfadder_8_c, halfadder_9_c, halfadder_10_c, halfadder_11_c, halfadder_12_c,
       halfadder_13_c, halfadder_14_c;

  halfadder halfadder_1 (.A(VAL_IN[1]), .B(1'b1), .S(VAL_OUT[1]), .C(halfadder_1_c));
  halfadder halfadder_2 (.A(VAL_IN[2]), .B(halfadder_1_c), .S(VAL_OUT[2]), .C(halfadder_2_c));
  halfadder halfadder_3 (.A(VAL_IN[3]), .B(halfadder_2_c), .S(VAL_OUT[3]), .C(halfadder_3_c));
  halfadder halfadder_4 (.A(VAL_IN[4]), .B(halfadder_3_c), .S(VAL_OUT[4]), .C(halfadder_4_c));
  halfadder halfadder_5 (.A(VAL_IN[5]), .B(halfadder_4_c), .S(VAL_OUT[5]), .C(halfadder_5_c));
  halfadder halfadder_6 (.A(VAL_IN[6]), .B(halfadder_5_c), .S(VAL_OUT[6]), .C(halfadder_6_c));
  halfadder halfadder_7 (.A(VAL_IN[7]), .B(halfadder_6_c), .S(VAL_OUT[7]), .C(halfadder_7_c));
  halfadder halfadder_8 (.A(VAL_IN[8]), .B(halfadder_7_c), .S(VAL_OUT[8]), .C(halfadder_8_c));
  halfadder halfadder_9 (.A(VAL_IN[9]), .B(halfadder_8_c), .S(VAL_OUT[9]), .C(halfadder_9_c));
  halfadder halfadder_10 (.A(VAL_IN[10]), .B(halfadder_9_c), .S(VAL_OUT[10]), .C(halfadder_10_c));
  halfadder halfadder_11 (.A(VAL_IN[11]), .B(halfadder_10_c), .S(VAL_OUT[11]), .C(halfadder_11_c));
  halfadder halfadder_12 (.A(VAL_IN[12]), .B(halfadder_11_c), .S(VAL_OUT[12]), .C(halfadder_12_c));
  halfadder halfadder_13 (.A(VAL_IN[13]), .B(halfadder_12_c), .S(VAL_OUT[13]), .C(halfadder_13_c));
  halfadder halfadder_14 (.A(VAL_IN[14]), .B(halfadder_13_c), .S(VAL_OUT[14]), .C(halfadder_14_c));
  halfadder halfadder_15 (.A(VAL_IN[15]), .B(halfadder_14_c), .S(VAL_OUT[15]));  // open: C

  assign VAL_OUT[0] = VAL_IN[0];
endmodule
