// Logisim project tower.circ as structural Verilog: 8 circuits, main circuit main
module main (
);

  ALU alu_1 ();  // open: A, B, SUBTRACT, SHIFT_LEFT, CIRCULAR_SHIFT, BOOL_OPCODE, OUTPUT_SELECT, FLAG_SELECT, FR_WE, CLK, FR_RESET, O
  REGFILE regfile_1 ();  // open: RESET, CLK, IN_DATA, IN_SEL, OUT_S_A, OUT_S_B, OUT_D_A, OUT_D_B
endmodule

module ALU (
  input  [15:0] A,
  input  [15:0] B,
  input  SUBTRACT,
  input  SHIFT_LEFT,
  input  CIRCULAR_SHIFT,
  input  [1:0] BOOL_OPCODE,
  input  [1:0] OUTPUT_SELECT,
  input  [1:0] FLAG_SELECT,
  input  FR_WE,
  input  CLK,
  input  FR_RESET,
  output [15:0] O
);

  wire and_1_out, C_q, fa_16_1_o, multiplexer_2_out, N_q, V_q, xor_2_out, Z_q;
  wire [15:0] bit_extender_1_out, bit_extender_2_out, bl_16_1_o, fa_16_1_s, not_1_out, sh_16_1_o, xor_1_out,
       xor_3_out;

  assign bit_extender_1_out = {{15{SUBTRACT}}, SUBTRACT};  // Bit_Extender bit_extender_1
  assign xor_1_out = B ^ bit_extender_1_out;  // XOR_Gate xor_1, 16 bits wide
  FA_16 fa_16_1 (.A(A), .B(xor_1_out), .C(SUBTRACT), .S(fa_16_1_s), .O(fa_16_1_o));
  SH_16 sh_16_1 (.I(A), .L(SHIFT_LEFT), .C(CIRCULAR_SHIFT), .O(sh_16_1_o));
  BL_16 bl_16_1 (.A(A), .B(B), .I(BOOL_OPCODE), .O(bl_16_1_o));
  and and_1 (and_1_out, not_1_out[8], not_1_out[15], not_1_out[14], not_1_out[13], not_1_out[12], not_1_out[11], not_1_out[10], not_1_out[9], not_1_out[7], not_1_out[6], not_1_out[5], not_1_out[4], not_1_out[3], not_1_out[2], not_1_out[1], not_1_out[0]);
  xor xor_2 (xor_2_out, fa_16_1_o, SUBTRACT);
  Multiplexer #(.select(2), .width(16)) multiplexer_1 (
    .in0(fa_16_1_s), .in1(sh_16_1_o), .in2(bl_16_1_o), .in3(bit_extender_2_out), .out(O), .sel(OUTPUT_SELECT));
  assign xor_3_out = {16{1'b0}} ^ O;  // XOR_Gate xor_3, 16 bits wide
  assign not_1_out = ~xor_3_out;  // NOT_Gate not_1, 16 bits wide
  Register #(.width(1)) V (.D(xor_2_out), .en(FR_WE), .clk(CLK), .Q(V_q), .clr(FR_RESET));
  Register #(.width(1)) C (.D(fa_16_1_o), .en(FR_WE), .clk(CLK), .Q(C_q), .clr(FR_RESET));
  Register #(.width(1)) N (.D(O[15]), .en(FR_WE), .clk(CLK), .Q(N_q), .clr(FR_RESET));
  Register #(.width(1)) Z (.D(and_1_out), .en(FR_WE), .clk(CLK), .Q(Z_q), .clr(FR_RESET));
  assign bit_extender_2_out = {{15{1'b0}}, multiplexer_2_out};  // Bit_Extender bit_extender_2
  Multiplexer #(.select(2)) multiplexer_2 (
    .in0(V_q), .in1(C_q), .in2(N_q), .in3(Z_q), .out(multiplexer_2_out), .sel(FLAG_SELECT));
endmodule

module FA_16 (
  input  [15:0] A,
  input  [15:0] B,
  input  C,
  output [15:0] S,
  output O
);

  wire fa_4_1_o, fa_4_2_o, fa_4_3_o;

  FA_4 fa_4_1 (.A(A[3:0]), .B(B[3:0]), .C(C), .S(S[3:0]), .O(fa_4_1_o));
  FA_4 fa_4_2 (.A(A[7:4]), .B(B[7:4]), .C(fa_4_1_o), .S(S[7:4]), .O(fa_4_2_o));
  FA_4 fa_4_3 (.A(A[11:8]), .B(B[11:8]), .C(fa_4_2_o), .S(S[11:8]), .O(fa_4_3_o));
  FA_4 fa_4_4 (.A(A[15:12]), .B(B[15:12]), .C(fa_4_3_o), .S(S[15:12]), .O(O));
endmodule

module FA_4 (
  input  [3:0] A,
  input  [3:0] B,
  input  C,
  output [3:0] S,
  output O
);

  wire fa_1_1_o, fa_1_2_o, fa_1_3_o;

  FA_1 fa_1_1 (.A(A[0]), .B(B[0]), .C(C), .S(S[0]), .O(fa_1_1_o));
  FA_1 fa_1_2 (.A(A[1]), .B(B[1]), .C(fa_1_1_o), .S(S[1]), .O(fa_1_2_o));
  FA_1 fa_1_3 (.A(A[2]), .B(B[2]), .C(fa_1_2_o), .S(S[2]), .O(fa_1_3_o));
  FA_1 fa_1_4 (.A(A[3]), .B(B[3]), .C(fa_1_3_o), .S(S[3]), .O(O));
endmodule

module FA_1 (
  input  A,
  input  B,
  input  C,
  output S,
  output O
);

  wire and_1_out, and_2_out, xor_1_out;

  xor xor_1 (xor_1_out, A, B);
  and and_1 (and_1_out, A, B);
  xor xor_2 (S, xor_1_out, C);
  and and_2 (and_2_out, xor_1_out, C);
  or or_1 (O, and_1_out, and_2_out);
endmodule

module SH_16 (
  input  [15:0] I,
  input  L,
  input  C,
  output [15:0] O
);

  Multiplexer #(.select(2), .width(16)) multiplexer_1 (
    .in0({1'b0, I[15:1]}), .in1({I[0], I[15:1]}), .in2({I[14:0], 1'b0}), .in3({I[14:0], I[15]}), .out(O),
    .sel({L, C}));
endmodule

module BL_16 (
  input  [15:0] A,
  input  [15:0] B,
  input  [1:0] I,
  output [15:0] O
);

  wire [15:0] and_1_out, not_1_out, or_1_out, xor_1_out;

  assign and_1_out = B & A;  // AND_Gate and_1, 16 bits wide
  assign or_1_out = B | A;  // OR_Gate or_1, 16 bits wide
  assign not_1_out = ~A;  // NOT_Gate not_1, 16 bits wide
  assign xor_1_out = B ^ A;  // XOR_Gate xor_1, 16 bits wide
  Multiplexer #(.select(2), .width(16)) multiplexer_1 (
    .in0(and_1_out), .in1(or_1_out), .in2(not_1_out), .in3(xor_1_out), .out(O), .sel(I));
endmodule

module REGFILE (
  input  RESET,
  input  CLK,
  input  [15:0] IN_DATA,
  input  [2:0] IN_SEL,
  input  [2:0] OUT_S_A,
  input  [2:0] OUT_S_B,
  output [15:0] OUT_D_A,
  output [15:0] OUT_D_B
);

  wire decoder_1_out0, decoder_1_out1, decoder_1_out2, decoder_1_out3, decoder_1_out4, decoder_1_out5,
       decoder_1_out6, decoder_1_out7;
  wire [15:0] A_q, B_q, C_q, D_q, E_q, F_q, G_q, H_q;

  Decoder #(.enable("false"), .select(3)) decoder_1 (
    .out0(decoder_1_out0), .out1(decoder_1_out1), .out2(decoder_1_out2), .out3(decoder_1_out3),
    .out4(decoder_1_out4), .out5(decoder_1_out5), .out6(decoder_1_out6), .out7(decoder_1_out7), .sel(IN_SEL));
  Register #(.width(16)) A (.D(IN_DATA), .en(decoder_1_out0), .clk(CLK), .Q(A_q), .clr(RESET));
  Register #(.width(16)) B (.D(IN_DATA), .en(decoder_1_out1), .clk(CLK), .Q(B_q), .clr(RESET));
  Register #(.width(16)) C (.D(IN_DATA), .en(decoder_1_out2), .clk(CLK), .Q(C_q), .clr(RESET));
  Register #(.width(16)) D (.D(IN_DATA), .en(decoder_1_out3), .clk(CLK), .Q(D_q), .clr(RESET));
  Register #(.width(16)) E (.D(IN_DATA), .en(decoder_1_out4), .clk(CLK), .Q(E_q), .clr(RESET));
  Register #(.width(16)) F (.D(IN_DATA), .en(decoder_1_out5), .clk(CLK), .Q(F_q), .clr(RESET));
  Register #(.width(16)) G (.D(IN_DATA), .en(decoder_1_out6), .clk(CLK), .Q(G_q), .clr(RESET));
  Register #(.width(16)) H (.D(IN_DATA), .en(decoder_1_out7), .clk(CLK), .Q(H_q), .clr(RESET));
  Multiplexer #(.select(3), .width(16)) multiplexer_1 (
    .in0(A_q), .in1(B_q), .in2(C_q), .in3(D_q), .in4(E_q), .in5(F_q), .in6(G_q), .in7(H_q), .out(OUT_D_A),
    .sel(OUT_S_A));
  Multiplexer #(.select(3), .width(16)) multiplexer_2 (
    .in0(A_q), .in1(B_q), .in2(C_q), .in3(D_q), .in4(E_q), .in5(F_q), .in6(G_q), .in7(H_q), .out(OUT_D_B),
    .sel(OUT_S_B));
endmodule
